# Fritzing sketch ControlPerfBoardMotor (saved by Fritzing 0.9.1b)
stripboards: 1

parts:
  Parte1 = Arduino Leonardo (Rev3b)
  VCC1 = Battery [part_number="Ultrafire 7,4V 6000mAH"]
  M1 = DC Motor
  M2 = DC Motor

nets:
  N1: Parte1.D0/RX, M1.pin_1
  N2: Parte1.D1/TX, M1.pin_2
  N3: Parte1.D2/SDA, M2.pin_2
  N4: Parte1.D3_PWM/SCL, M2.pin_1
  N5: Parte1.GND, VCC1.-
  N6: Parte1.VIN, VCC1.+

notes:
  Azul: B
  Amarillo: F
  Blanco: L
  Verde: R

// code stored in the sketch: Control.ino
int ledPin = 2;                 // LED connected to digital pin 13

void setup()
{
  pinMode(ledPin, OUTPUT);      // sets the digital pin as output
}

void loop()
{
  digitalWrite(ledPin, HIGH);   // sets the LED on
  delay(2000);                  // waits for a second
  digitalWrite(ledPin, LOW);    // sets the LED off
  delay(2000);                  // waits for a second
}
