# Fritzing sketch ControlProtoBoardMotor (saved by Fritzing 0.9.1b)
breadboards: 1

parts:
  Parte1 = Arduino Leonardo (Rev3b)
  R2 = Resistor [tolerance=±5% resistance=100 package=THT]
  R1 = Resistor [tolerance=±5% resistance=100 package=THT]
  R4 = Resistor [tolerance=±5% resistance=100 package=THT]
  R3 = Resistor [tolerance=±5% resistance=100 package=THT]
  LED2 = LED - 3mm [color="Yellow (595nm)" package="3 mm [THT]"]
  LED1 = LED - 3mm [color="Blue (525nm)" package="3 mm [THT]"]
  LED3 = LED - 3mm [color="White (4500K)" package="3 mm [THT]"]
  LED4 = LED - 3mm [color="Green (570nm)" package="3 mm [THT]"]
  VCC1 = Battery [part_number="Ultrafire 7,4V 6000mAH"]
  M1 = DC Motor
  M2 = DC Motor

nets:
  N1: Parte1.D2/SDA, Parte1.SDA, R1.Pin_1, M1.pin_1
  N2: Parte1.D3_PWM/SCL, Parte1.SCL, R2.Pin_1, M1.pin_2
  N3: Parte1.D4/A6, R3.Pin_1, M2.pin_2
  N4: Parte1.D5_PWM, R4.Pin_1, M2.pin_1
  N5: Parte1.GND, VCC1.-
  N6: Parte1.VIN, VCC1.+
  N7: R2.Pin_0, LED2.cathode, LED1.anode
  N8: R1.Pin_0, LED2.anode, LED1.cathode
  N9: R4.Pin_0, LED3.cathode, LED4.anode
  N10: R3.Pin_0, LED3.anode, LED4.cathode

notes:
  Azul: B
  Amarillo: F
  Blanco: L
  Verde: R

// code stored in the sketch: Control.ino
int ledPin = 2;                 // LED connected to digital pin 13

void setup()
{
  pinMode(ledPin, OUTPUT);      // sets the digital pin as output
}

void loop()
{
  digitalWrite(ledPin, HIGH);   // sets the LED on
  delay(2000);                  // waits for a second
  digitalWrite(ledPin, LOW);    // sets the LED off
  delay(2000);                  // waits for a second
}
